// Logisim project CircuitDesignFinal.circ as structural Verilog: 1 circuit, main circuit main
module main (
  input  Enable,
  input  x2,
  input  x1,
  input  x0,
  input  Piece,
  input  y2,
  input  y1,
  input  y0,
  output Right,
  output Left,
  output [2:0] X,
  output [2:0] Y,
  output Up,
  output Down
);

  wire a0_2_qn, a0_qn, a1_2_qn, a1_qn, and_1_out, and_2_out, and_3_out, and_4_out, and_5_out, and_6_out,
       and_7_out, and_8_out, and_9_out, and_10_out, and_11_out, clock_1_out, comparator_1_eq,
       comparator_1_gt, comparator_1_lt, comparator_2_eq, comparator_2_gt, comparator_2_lt, comparator_3_eq,
       comparator_4_eq, comparator_6_gt, comparator_6_lt, multiplexer_1_out, multiplexer_2_out,
       multiplexer_3_out, not_1_out, not_2_out, not_3_out, not_4_out, not_5_out, not_6_out, not_7_out,
       not_8_out, not_9_out, not_10_out, or_1_out, or_2_out, Reset_out, subtractor_1_bout, subtractor_2_bout,
       xnor_1_out;
  wire [1:0] priority_encoder_1_out, priority_encoder_2_out;
  wire [2:0] a0_2_q, a0_q, adder_1_out, subtractor_1_out, subtractor_2_out;

  Button Reset (.out(Reset_out));
  Comparator #(.width(3), .mode("unsigned")) comparator_1 (
    .a(a0_q), .b({x2, x1, x0}), .gt(comparator_1_gt), .eq(comparator_1_eq), .lt(comparator_1_lt));
  Subtractor #(.width(3)) subtractor_1 (
    .a(a0_q), .b({x2, x1, x0}), .out(subtractor_1_out), .bout(subtractor_1_bout));  // open: bin
  xnor xnor_1 (xnor_1_out, subtractor_1_bout, subtractor_2_bout);
  Subtractor #(.width(3)) subtractor_2 (
    .a(a0_2_q), .b({y2, y1, y0}), .out(subtractor_2_out), .bout(subtractor_2_bout));  // open: bin
  Comparator #(.width(3), .mode("unsigned")) comparator_2 (
    .a(a0_2_q), .b({y2, y1, y0}), .gt(comparator_2_gt), .eq(comparator_2_eq), .lt(comparator_2_lt));
  Adder #(.width(3)) adder_1 (.a(subtractor_1_out), .b(subtractor_2_out), .out(adder_1_out));  // open: cin, cout
  Comparator #(.width(3)) comparator_3 (.a(adder_1_out), .b(3'b000), .eq(comparator_3_eq));  // open: gt, lt
  Comparator #(.width(3)) comparator_4 (
    .a(subtractor_1_out), .b(subtractor_2_out), .eq(comparator_4_eq));  // open: gt, lt
  not not_1 (not_1_out, comparator_1_eq);
  Multiplexer multiplexer_1 (
    .in0(comparator_3_eq), .in1(comparator_4_eq), .out(multiplexer_1_out), .sel(xnor_1_out));  // open: en
  not not_2 (not_2_out, multiplexer_1_out);
  not not_3 (not_3_out, comparator_2_eq);
  and and_1 (and_1_out, not_1_out, not_2_out, not_3_out);
  and and_2 (and_2_out, not_2_out, not_1_out, not_3_out);
  Multiplexer multiplexer_2 (.in0(and_1_out), .in1(not_3_out), .out(multiplexer_2_out), .sel(Piece));  // open: en
  Multiplexer multiplexer_3 (.in0(and_2_out), .in1(not_1_out), .out(multiplexer_3_out), .sel(Piece));  // open: en
  Priority_Encoder #(.select(2)) priority_encoder_1 (
    .in0(comparator_1_gt), .in1(comparator_1_eq), .in2(comparator_1_lt), .in3(multiplexer_2_out),
    .out(priority_encoder_1_out));  // open: gs, en_out, en_in
  not not_4 (not_4_out, priority_encoder_1_out[0]);
  not not_5 (not_5_out, priority_encoder_1_out[1]);
  Priority_Encoder #(.select(2)) priority_encoder_2 (
    .in0(comparator_2_gt), .in1(comparator_2_eq), .in2(comparator_2_lt), .in3(multiplexer_3_out),
    .out(priority_encoder_2_out));  // open: gs, en_out, en_in
  not not_6 (not_6_out, priority_encoder_2_out[0]);
  not not_7 (not_7_out, priority_encoder_2_out[1]);
  and and_3 (and_3_out, priority_encoder_1_out[1], not_4_out, a0_q[0]);
  and and_4 (and_4_out, not_5_out, not_4_out, a0_qn);
  and and_5 (and_5_out, priority_encoder_2_out[1], not_6_out, a0_2_q[0]);
  and and_6 (and_6_out, not_7_out, not_6_out, a0_2_qn);
  Clock clock_1 (.out(clock_1_out));
  and and_7 (and_7_out, and_3_out, a0_q[1]);
  and and_8 (and_8_out, a1_qn, and_4_out);
  or or_1 (or_1_out, and_3_out, and_4_out);
  and and_9 (and_9_out, and_5_out, a0_2_q[1]);
  and and_10 (and_10_out, a1_2_qn, and_6_out);
  or or_2 (or_2_out, and_5_out, and_6_out);
  and and_11 (and_11_out, clock_1_out, Enable);
  J_K_Flip_Flop a2 (
    .J(and_7_out), .clk(and_11_out), .K(and_8_out), .Q(a0_q[2]), .reset(Reset_out));  // open: Qn, preset, en
  J_K_Flip_Flop a1 (
    .J(or_1_out), .clk(and_11_out), .K(or_1_out), .Q(a0_q[1]), .Qn(a1_qn), .reset(Reset_out));  // open: preset, en
  J_K_Flip_Flop a0 (
    .J(not_4_out), .clk(and_11_out), .K(not_4_out), .Q(a0_q[0]), .Qn(a0_qn), .reset(Reset_out));  // open: preset, en
  J_K_Flip_Flop a2_2 (
    .J(and_9_out), .clk(and_11_out), .K(and_10_out), .Q(a0_2_q[2]), .reset(Reset_out));  // open: Qn, preset, en
  J_K_Flip_Flop a1_2 (
    .J(or_2_out), .clk(and_11_out), .K(or_2_out), .Q(a0_2_q[1]), .Qn(a1_2_qn), .reset(Reset_out));  // open: preset, en
  J_K_Flip_Flop a0_2 (
    .J(not_6_out), .clk(and_11_out), .K(not_6_out), .Q(a0_2_q[0]), .Qn(a0_2_qn), .reset(Reset_out));  // open: preset, en
  Register #(.width(3)) register_1 (.D(a0_q), .Q(X), .clk(not_8_out));  // open: en, clr
  not not_8 (not_8_out, and_11_out);
  Register #(.width(3)) register_2 (.D(a0_2_q), .Q(Y), .clk(and_11_out));  // open: en, clr
  not not_9 (not_9_out, and_11_out);
  not not_10 (not_10_out, and_11_out);
  Comparator #(.width(3), .mode("unsigned")) comparator_5 (.a(a0_q), .b(X), .gt(Right), .lt(Left));  // open: eq
  Comparator #(.width(3), .mode("unsigned")) comparator_6 (
    .a(a0_2_q), .b(Y), .gt(comparator_6_gt), .lt(comparator_6_lt));  // open: eq
  and and_12 (Up, comparator_6_gt, not_9_out);
  and and_13 (Down, comparator_6_lt, not_10_out);
endmodule
